// Logisim project projeto-gtn-xtreme.circ as structural Verilog: 13 circuits, main circuit main
module main (
  input  in_1,
  input  in_2
);

  wire clk, FIM_A, M0a, M1a, Reset, S0a, S1a;
  wire [3:0] m0, m1, s0, s1;

  Button button_1 (.out(Reset));
  LED led_1 (.in(in_2));
  Hex_Digit_Display hex_digit_display_1 (.value(m1));  // open: dp
  Hex_Digit_Display hex_digit_display_2 (.value(m0));  // open: dp
  Button button_2 (.out(M1a));
  Button button_3 (.out(M0a));
  Hex_Digit_Display hex_digit_display_3 (.value(s1));  // open: dp
  Button button_4 (.out(S1a));
  Hex_Digit_Display hex_digit_display_4 (.value(s0));  // open: dp
  Button button_5 (.out(S0a));
  Cronometro cronometro_1 (
    .clk(clk), .jogando(in_2), .cfg(in_1), .reset(Reset), .s0(S0a), .s1(S1a), .m0(M0a), .m1(M1a),
    .FimC(FIM_A), .S0c(s0), .S1c(s1), .M0c(m0), .M1c(m1));
  Clock clock_1 (.out(clk));

  // Other names for the same wires on the sheet: A_jogando = in_2; cfg = in_1
endmodule

module Registrador4 (
  input  [3:0] D,
  input  Enable,
  input  Clock,
  input  Reset,
  output [3:0] Q
);

  Register #(.width(4), .Select("low")) register_1 (.D(D), .en(Enable), .Q(Q), .clk(Clock), .clr(Reset));
endmodule

module Contador (
  input  Enable,
  input  Clock,
  input  Reset,
  output [3:0] out_4
);

  Counter #(.width(4), .max('h9)) counter_1 (
    .count(Enable), .Q(out_4), .clk(Clock), .clr(Reset), .down(1'b1));  // open: load, D, carry, preset
endmodule

module Somador4b5b (
  input  [3:0] A,
  input  [3:0] B,
  output [4:0] out_3
);

  Adder #(.width(4)) adder_1 (.a(A), .b(B), .out(out_3[3:0]), .cout(out_3[4]));  // open: cin
endmodule

module Comparador_5b (
  input  [4:0] A,
  input  [4:0] B,
  output Igual
);

  Comparator #(.width(5)) comparator_1 (.a(A), .b(B), .eq(Igual));  // open: gt, lt
endmodule

module Diferenca_5b (
  input  [4:0] A,
  input  [4:0] B,
  output [4:0] DIFF
);

  wire SEL;
  wire [4:0] DAB, DBA;

  Multiplexer #(.width(5), .enable("false")) multiplexer_1 (.in0(DAB), .in1(DBA), .out(DIFF), .sel(SEL));
  Subtractor #(.width(5)) subtractor_1 (.a(A), .b(B), .out(DAB), .bin(1'b0), .bout(SEL));
  Subtractor #(.width(5)) subtractor_2 (.a(B), .b(A), .out(DBA), .bin(1'b0));  // open: bout
endmodule

module cores_5b (
  input  [4:0] a,
  output [7:0] out_2,
  output [7:0] out_3
);

  wire [7:0] bit_extender_1_out, shifter_1_out;

  assign bit_extender_1_out = {{3{1'b0}}, a};  // Bit_Extender bit_extender_1
  Shifter shifter_1 (.in(bit_extender_1_out), .\dist (3'b011), .out(shifter_1_out));
  assign out_2 = shifter_1_out | 8'h7;  // OR_Gate or_1, 8 bits wide
  assign out_3 = ~out_2;  // NOT_Gate not_1, 8 bits wide
endmodule

module comparador_4b (
  input  [3:0] A,
  input  [3:0] B,
  output Igual
);

  Comparator #(.width(4)) comparator_1 (.a(A), .b(B), .eq(Igual));  // open: gt, lt
endmodule

module GTN_X (
  input  Confirmar,
  input  Novo,
  input  [3:0] X,
  input  [3:0] Y,
  output [7:0] r,
  output [7:0] b,
  output X_2,
  output Y_2,
  output S
);

  wire comparador_4b_1_igual, comparador_4b_2_igual, comparador_5b_1_igual;
  wire [4:0] diferenca_5b_1_diff, somador4b5b_1_out_3, somador4b5b_2_out_3;
  wire [7:0] bit_extender_1_out, cores_5b_1_out_2, cores_5b_1_out_3, random_1_out;

  Random random_1 (.clk(Novo), .out(random_1_out));  // open: next, clr
  assign bit_extender_1_out = {{7{Confirmar}}, Confirmar};  // Bit_Extender bit_extender_1
  and and_1 (X_2, Confirmar, comparador_4b_1_igual);
  comparador_4b comparador_4b_1 (.A(random_1_out[7:4]), .B(X), .Igual(comparador_4b_1_igual));
  Somador4b5b somador4b5b_1 (.A(random_1_out[3:0]), .B(random_1_out[7:4]), .out_3(somador4b5b_1_out_3));
  Somador4b5b somador4b5b_2 (.A(Y), .B(X), .out_3(somador4b5b_2_out_3));
  and and_2 (Y_2, Confirmar, comparador_4b_2_igual);
  and and_3 (S, Confirmar, comparador_5b_1_igual);
  Comparador_5b comparador_5b_1 (.A(somador4b5b_1_out_3), .B(somador4b5b_2_out_3), .Igual(comparador_5b_1_igual));
  comparador_4b comparador_4b_2 (.A(random_1_out[3:0]), .B(Y), .Igual(comparador_4b_2_igual));
  assign r = bit_extender_1_out & cores_5b_1_out_2;  // AND_Gate and_4, 8 bits wide
  Diferenca_5b diferenca_5b_1 (.A(somador4b5b_1_out_3), .B(somador4b5b_2_out_3), .DIFF(diferenca_5b_1_diff));
  assign b = cores_5b_1_out_3 & bit_extender_1_out;  // AND_Gate and_5, 8 bits wide
  cores_5b cores_5b_1 (.a(diferenca_5b_1_diff), .out_2(cores_5b_1_out_2), .out_3(cores_5b_1_out_3));
endmodule

module Digito (
  input  clk,
  input  BTN,
  input  EN,
  input  cfg,
  input  RESET,
  input  [3:0] MAX,
  output [3:0] Q,
  output ZERO
);

  wire ATMAX, clkd, enr;
  wire [3:0] D, Dcfg, DEC, Drun, INC;

  Multiplexer #(.width(4)) multiplexer_1 (.in0(DEC), .in1(MAX), .out(Drun), .sel(ZERO));  // open: en
  Multiplexer #(.width(4)) multiplexer_2 (.in0(INC), .in1(4'b0000), .out(Dcfg), .sel(ATMAX));  // open: en
  Adder #(.width(4)) adder_1 (.a(Q), .b(4'b0001), .out(INC), .cin(1'b0));  // open: cout
  Subtractor #(.width(4)) subtractor_1 (.a(Q), .b(4'b0001), .out(DEC), .bin(1'b0));  // open: bout
  Comparator #(.width(4)) comparator_1 (.a(Q), .b(4'b0000), .eq(ZERO));  // open: gt, lt
  Comparator #(.width(4)) comparator_2 (.a(Q), .b(MAX), .eq(ATMAX));  // open: gt, lt
  Multiplexer #(.width(4)) multiplexer_3 (.in0(Drun), .in1(Dcfg), .out(D), .sel(cfg));  // open: en
  Multiplexer multiplexer_4 (.in0(clk), .in1(BTN), .out(clkd), .sel(cfg));  // open: en
  Multiplexer multiplexer_5 (.in0(EN), .in1(1'b1), .out(enr), .sel(cfg));  // open: en
  Register #(.width(4), .Select("low")) Qreg (.D(D), .en(enr), .Q(Q), .clk(clkd), .clr(RESET));
endmodule

module Cronometro (
  input  clk,
  input  jogando,
  input  cfg,
  input  reset,
  input  s0,
  input  s1,
  input  m0,
  input  m1,
  output FimC,
  output [3:0] S0c,
  output [3:0] S1c,
  output [3:0] M0c,
  output [3:0] M1c
);

  wire EN_M0, EN_M1, EN_S1, G, NCFG, NFIM, Z_M0, Z_M1, Z_S0, Z_S1;

  Digito Dig_S0 (.clk(clk), .BTN(s0), .EN(G), .cfg(cfg), .RESET(reset), .MAX(4'b1001), .Q(S0c), .ZERO(Z_S0));
  Digito Dig_S1 (.clk(clk), .BTN(s1), .EN(EN_S1), .cfg(cfg), .RESET(reset), .MAX(4'b0101), .Q(S1c), .ZERO(Z_S1));
  not not_1 (NCFG, cfg);
  not not_2 (NFIM, FimC);
  Digito Dig_M0 (.clk(clk), .BTN(m0), .EN(EN_M0), .cfg(cfg), .RESET(reset), .MAX(4'b1001), .Q(M0c), .ZERO(Z_M0));
  Digito Dig_M1 (.clk(clk), .BTN(m1), .EN(EN_M1), .cfg(cfg), .RESET(reset), .MAX(4'b0101), .Q(M1c), .ZERO(Z_M1));
  and and_1 (G, jogando, NCFG, NFIM);
  and and_2 (EN_S1, G, Z_S0);
  and and_3 (EN_M0, G, Z_S0, Z_S1);
  and and_4 (EN_M1, G, Z_S0, Z_S1, Z_M0);
  and and_5 (FimC, Z_S0, Z_S1, Z_M0, Z_M1);

  // Other names for the same wires on the sheet: FIM = FimC; JOG = jogando; Q_M0[3:0] = M0c; Q_M1[3:0] = M1c;
  //   Q_S0[3:0] = S0c; Q_S1[3:0] = S1c
endmodule

module CORE (
  input  C_A,
  input  C_B,
  input  [3:0] V_A,
  input  [3:0] V_B,
  input  jogando,
  input  fim_A,
  input  fim_B,
  input  Avancar,
  input  Acerto,
  input  Reset,
  output A_jogando,
  output [7:0] r,
  output [7:0] b,
  output B_jogando,
  output Soma_certa,
  output X_certo,
  output Y_certo,
  output [3:0] X_atual,
  output [3:0] Y_atual,
  output Jogando_X,
  output Jogando_Y
);

  wire or_1_out;
  wire [3:0] multiplexer_1_out, multiplexer_2_out;

  or or_1 (or_1_out, C_A, C_B);
  Multiplexer #(.width(4), .enable("false")) multiplexer_1 (
    .in0(V_A), .in1(V_B), .out(multiplexer_1_out));  // open: sel
  Multiplexer #(.width(4), .enable("false")) multiplexer_2 (
    .in0(V_A), .in1(V_B), .out(multiplexer_2_out));  // open: sel
  Registrador4 Registrador4_X (.D(multiplexer_1_out), .Clock(or_1_out), .Q(X_atual), .Reset(Reset));  // open: Enable
  Registrador4 Registrador4_Y (.D(multiplexer_2_out), .Clock(or_1_out), .Q(Y_atual), .Reset(Reset));  // open: Enable
  GTN_X GTN_X (.X(X_atual), .Y(Y_atual));  // open: Confirmar, Novo, X_2, Y_2, S, r, b
endmodule

module ESTADO_CORE (
  input  Avancar,
  input  Reset,
  output [2:0] Estado_atual
);

  wire D0, D1, D2, E0, E1, E2, E3, E4, E5, E6, E7;
  wire [3:0] bit_extender_1_out;

  Register #(.width(3), .Select("low")) Estado (
    .D({D2, D1, D0}), .en(1'b1), .Q(Estado_atual), .clk(Avancar), .clr(Reset));
  Multiplexer #(.select(3), .enable("false")) multiplexer_1 (
    .in0(1'b1), .in1(1'b0), .in2(1'b1), .in3(1'b0), .in4(1'b1), .in5(1'b0), .in6(1'b1), .in7(1'b1), .out(D0),
    .sel(Estado_atual));
  assign bit_extender_1_out = {{1{1'b0}}, Estado_atual};  // Bit_Extender bit_extender_1
  Multiplexer #(.select(3), .enable("false")) multiplexer_2 (
    .in0(1'b0), .in1(1'b1), .in2(1'b1), .in3(1'b0), .in4(1'b0), .in5(1'b1), .in6(1'b0), .in7(1'b1), .out(D1),
    .sel(Estado_atual));
  Hex_Digit_Display hex_digit_display_1 (.value(bit_extender_1_out));  // open: dp
  Multiplexer #(.select(3), .enable("false")) multiplexer_3 (
    .in0(1'b0), .in1(1'b0), .in2(1'b0), .in3(1'b1), .in4(1'b1), .in5(1'b1), .in6(1'b0), .in7(1'b1), .out(D2),
    .sel(Estado_atual));
  Decoder #(.select(3), .enable("false")) decoder_1 (
    .out0(E0), .out1(E1), .out2(E2), .out3(E3), .out4(E4), .out5(E5), .out6(E6), .out7(E7), .sel(Estado_atual));

  // Other names for the same wires on the sheet: Q[2:0] = Estado_atual
endmodule
